# Fritzing sketch scene (saved by Fritzing 0.9.3b)
breadboards: 1

parts:
  Part1 = Arduino Uno (Rev3)
  RHT1 = Humidity and Temperature Sensor RHT03
  R1 = Photocell (LDR) [package=THT]  # not connected
  VCC1 = 4 x AAA Battery Mount  # not connected

nets:
  N1: Part1.D4, RHT1.Data-signal
  5V: Part1.5V, RHT1.Vcc
  N2: Part1.GND, RHT1.GND_2
